// Logisim project control.circ as structural Verilog: 1 circuit, main circuit k
module k (
  input  st,
  input  lsb,
  input  comp,
  input  clock,
  output load,
  output add,
  output shift,
  output done
);

  wire and_1_out, and_2_out, and_5_out, and_7_out, J0K0_q, J0K0_qn, J1K1_q, J1K1_qn, not_1_out, not_3_out,
       or_1_out, or_2_out, or_3_out, or_4_out;

  not not_1 (not_1_out, lsb);
  // NOT_Gate not_2 has open pins: in=st, out=open
  not not_3 (not_3_out, comp);
  and and_1 (and_1_out, lsb, J0K0_q);
  and and_2 (and_2_out, comp, J0K0_q);
  or or_1 (or_1_out, and_1_out, and_2_out);
  or or_2 (or_2_out, not_3_out, J0K0_q);
  or or_3 (or_3_out, st, J1K1_q);
  or or_4 (or_4_out, lsb, J1K1_q);
  J_K_Flip_Flop J1K1 (.J(or_1_out), .clk(clock), .K(or_2_out), .Q(J1K1_q), .Qn(J1K1_qn));  // open: preset, en, reset
  J_K_Flip_Flop J0K0 (.J(or_3_out), .clk(clock), .K(or_4_out), .Q(J0K0_q), .Qn(J0K0_qn));  // open: preset, en, reset
  and and_3 (load, st, J1K1_qn, J0K0_qn);
  or or_5 (shift, and_5_out, and_7_out);
  and and_4 (add, J1K1_qn, J0K0_q, lsb);
  and and_5 (and_5_out, J1K1_q, J0K0_qn);
  and and_6 (done, J1K1_q, J0K0_q);
  and and_7 (and_7_out, not_1_out, J1K1_qn, J0K0_q);
endmodule
