// Logisim project datapath.circ as structural Verilog: 5 circuits, main circuit main
module main (
  input  A,
  input  B,
  input  Cin,
  output Sum,
  output Cout
);

  wire and_1_out, and_2_out, xor_1_out;

  xor xor_1 (xor_1_out, A, B);
  xor xor_2 (Sum, xor_1_out, Cin);
  and and_1 (and_1_out, Cin, xor_1_out);
  and and_2 (and_2_out, A, B);
  or or_1 (Cout, and_1_out, and_2_out);

  // Notes on the sheet:
  //   Full adder
endmodule

module FullAdder (
  input  [31:0] A,
  input  [31:0] B,
  output [31:0] Out
);

  wire main_1_cout, main_2_cout, main_3_cout, main_4_cout, main_5_cout, main_6_cout, main_7_cout,
       main_8_cout, main_9_cout, main_10_cout, main_11_cout, main_12_cout, main_13_cout, main_14_cout,
       main_15_cout, main_16_cout, main_17_cout, main_18_cout, main_19_cout, main_20_cout, main_21_cout,
       main_22_cout, main_23_cout, main_24_cout, main_25_cout, main_26_cout, main_27_cout, main_28_cout,
       main_29_cout, main_30_cout, main_31_cout;

  main main_1 (.A(A[0]), .B(B[0]), .Cin(1'b0), .Sum(Out[0]), .Cout(main_1_cout));
  main main_2 (.A(A[1]), .B(B[1]), .Cin(main_1_cout), .Sum(Out[1]), .Cout(main_2_cout));
  main main_3 (.A(A[2]), .B(B[2]), .Cin(main_2_cout), .Sum(Out[2]), .Cout(main_3_cout));
  main main_4 (.A(A[3]), .B(B[3]), .Cin(main_3_cout), .Sum(Out[3]), .Cout(main_4_cout));
  main main_5 (.A(A[4]), .B(B[4]), .Cin(main_4_cout), .Sum(Out[4]), .Cout(main_5_cout));
  main main_6 (.A(A[5]), .B(B[5]), .Cin(main_5_cout), .Sum(Out[5]), .Cout(main_6_cout));
  main main_7 (.A(A[6]), .B(B[6]), .Cin(main_6_cout), .Sum(Out[6]), .Cout(main_7_cout));
  main main_8 (.A(A[7]), .B(B[7]), .Cin(main_7_cout), .Sum(Out[7]), .Cout(main_8_cout));
  main main_9 (.A(A[8]), .B(B[8]), .Cin(main_8_cout), .Sum(Out[8]), .Cout(main_9_cout));
  main main_10 (.A(A[9]), .B(B[9]), .Cin(main_9_cout), .Sum(Out[9]), .Cout(main_10_cout));
  main main_11 (.A(A[10]), .B(B[10]), .Cin(main_10_cout), .Sum(Out[10]), .Cout(main_11_cout));
  main main_12 (.A(A[11]), .B(B[11]), .Cin(main_11_cout), .Sum(Out[11]), .Cout(main_12_cout));
  main main_13 (.A(A[12]), .B(B[12]), .Cin(main_12_cout), .Sum(Out[12]), .Cout(main_13_cout));
  main main_14 (.A(A[13]), .B(B[13]), .Cin(main_13_cout), .Sum(Out[13]), .Cout(main_14_cout));
  main main_15 (.A(A[14]), .B(B[14]), .Cin(main_14_cout), .Sum(Out[14]), .Cout(main_15_cout));
  main main_16 (.A(A[15]), .B(B[15]), .Cin(main_15_cout), .Sum(Out[15]), .Cout(main_16_cout));
  main main_17 (.A(A[16]), .B(B[16]), .Cin(main_16_cout), .Sum(Out[16]), .Cout(main_17_cout));
  main main_18 (.A(A[17]), .B(B[17]), .Cin(main_17_cout), .Sum(Out[17]), .Cout(main_18_cout));
  main main_19 (.A(A[18]), .B(B[18]), .Cin(main_18_cout), .Sum(Out[18]), .Cout(main_19_cout));
  main main_20 (.A(A[19]), .B(B[19]), .Cin(main_19_cout), .Sum(Out[19]), .Cout(main_20_cout));
  main main_21 (.A(A[20]), .B(B[20]), .Cin(main_20_cout), .Sum(Out[20]), .Cout(main_21_cout));
  main main_22 (.A(A[21]), .B(B[21]), .Cin(main_21_cout), .Sum(Out[21]), .Cout(main_22_cout));
  main main_23 (.A(A[22]), .B(B[22]), .Cin(main_22_cout), .Sum(Out[22]), .Cout(main_23_cout));
  main main_24 (.A(A[23]), .B(B[23]), .Cin(main_23_cout), .Sum(Out[23]), .Cout(main_24_cout));
  main main_25 (.A(A[24]), .B(B[24]), .Cin(main_24_cout), .Sum(Out[24]), .Cout(main_25_cout));
  main main_26 (.A(A[25]), .B(B[25]), .Cin(main_25_cout), .Sum(Out[25]), .Cout(main_26_cout));
  main main_27 (.A(A[26]), .B(B[26]), .Cin(main_26_cout), .Sum(Out[26]), .Cout(main_27_cout));
  main main_28 (.A(A[27]), .B(B[27]), .Cin(main_27_cout), .Sum(Out[27]), .Cout(main_28_cout));
  main main_29 (.A(A[28]), .B(B[28]), .Cin(main_28_cout), .Sum(Out[28]), .Cout(main_29_cout));
  main main_30 (.A(A[29]), .B(B[29]), .Cin(main_29_cout), .Sum(Out[29]), .Cout(main_30_cout));
  main main_31 (.A(A[30]), .B(B[30]), .Cin(main_30_cout), .Sum(Out[30]), .Cout(main_31_cout));
  main main_32 (.A(A[31]), .B(B[31]), .Cin(main_31_cout), .Sum(Out[31]));  // open: Cout

  // Other names for the same wires on the sheet: A1 = A[0]; A2 = A[1]; A3 = A[2]; A4 = A[3]; A5 = A[4]; A6 = A[5];
  //   A7 = A[6]; A8 = A[7]; A9 = A[8]; A10 = A[9]; A11 = A[10]; A12 = A[11]; A13 = A[12]; A14 = A[13]; A15 = A[14];
  //   A16 = A[15]; A17 = A[16]; A18 = A[17]; A19 = A[18]; A20 = A[19]; A21 = A[20]; A22 = A[21]; A23 = A[22];
  //   A24 = A[23]; A25 = A[24]; A26 = A[25]; A27 = A[26]; A28 = A[27]; A29 = A[28]; A30 = A[29]; A31 = A[30];
  //   A32 = A[31]; B1 = B[0]; B2 = B[1]; B3 = B[2]; B4 = B[3]; B5 = B[4]; B6 = B[5]; B7 = B[6]; B8 = B[7]; B9 = B[8];
  //   B10 = B[9]; B11 = B[10]; B12 = B[11]; B13 = B[12]; B14 = B[13]; B15 = B[14]; B16 = B[15]; B17 = B[16];
  //   B18 = B[17]; B19 = B[18]; B20 = B[19]; B21 = B[20]; B22 = B[21]; B23 = B[22]; B24 = B[23]; B25 = B[24];
  //   B26 = B[25]; B27 = B[26]; B28 = B[27]; B29 = B[28]; B30 = B[29]; B31 = B[30]; B32 = B[31]; S1 = Out[0];
  //   S2 = Out[1]; S3 = Out[2]; S4 = Out[3]; S5 = Out[4]; S6 = Out[5]; S7 = Out[6]; S8 = Out[7]; S9 = Out[8];
  //   S10 = Out[9]; S11 = Out[10]; S12 = Out[11]; S13 = Out[12]; S14 = Out[13]; S15 = Out[14]; S16 = Out[15];
  //   S17 = Out[16]; S18 = Out[17]; S19 = Out[18]; S20 = Out[19]; S21 = Out[20]; S22 = Out[21]; S23 = Out[22];
  //   S24 = Out[23]; S25 = Out[24]; S26 = Out[25]; S27 = Out[26]; S28 = Out[27]; S29 = Out[28]; S30 = Out[29];
  //   S31 = Out[30]; S32 = Out[31]
endmodule

module ALU (
  input  C1,
  input  [31:0] A,
  input  [31:0] B,
  output [31:0] Out
);

  wire [31:0] fulladder_1_out;

  FullAdder fulladder_1 (.A(A), .B(B), .Out(fulladder_1_out));
  Multiplexer #(.width(32), .enable("false")) multiplexer_1 (.in0(B), .in1(fulladder_1_out), .out(Out), .sel(C1));
endmodule

module Datapath (
  input  [31:0] Multiplicand,
  input  [31:0] Multiplier,
  input  clock,
  input  add,
  input  shift,
  input  load,
  output comp,
  output lsb,
  output [31:0] out_9,
  output [31:0] out_10
);

  wire or_1_out;
  wire [31:0] alu_1_out, multiplexer_1_out, multiplexer_2_out, right_shifter_1_out, right_shifter_1_out_2;

  ALU alu_1 (.C1(add), .A(out_10), .B(Multiplicand), .Out(alu_1_out));
  Right_Shifter right_shifter_1 (
    .Select(shift), .A({out_9[31:1], lsb}), .B(alu_1_out), .out(right_shifter_1_out),
    .out_2(right_shifter_1_out_2));
  Multiplexer #(.width(32), .enable("false")) multiplexer_1 (
    .in0(right_shifter_1_out_2), .in1(Multiplicand), .out(multiplexer_1_out), .sel(load));
  Multiplexer #(.width(32), .enable("false")) multiplexer_2 (
    .in0(right_shifter_1_out), .in1(Multiplier), .out(multiplexer_2_out), .sel(load));
  Register #(.width(32)) register_1 (
    .D(multiplexer_2_out), .en(or_1_out), .Q({out_9[31:1], lsb}), .clk(clock));  // open: clr
  Register #(.width(32)) register_2 (.D(multiplexer_1_out), .en(or_1_out), .Q(out_10), .clk(clock));  // open: clr
  Counter counter_1 (.count(shift), .carry(comp), .clk(clock));  // open: load, D, Q, clr
  or or_1 (or_1_out, shift, load);

  assign out_9[0] = lsb;
endmodule

module Right_Shifter (
  input  Select,
  input  [31:0] A,
  input  [31:0] B,
  output [31:0] out,
  output [31:0] out_2
);

  Multiplexer #(.enable("false")) multiplexer_1 (.in0(A[0]), .in1(A[1]), .out(out[0]), .sel(Select));
  Multiplexer #(.enable("false")) multiplexer_2 (.in0(A[1]), .in1(A[2]), .out(out[1]), .sel(Select));
  Multiplexer #(.enable("false")) multiplexer_3 (.in0(A[2]), .in1(A[3]), .out(out[2]), .sel(Select));
  Multiplexer #(.enable("false")) multiplexer_4 (.in0(A[3]), .in1(A[4]), .out(out[3]), .sel(Select));
  Multiplexer #(.enable("false")) multiplexer_5 (.in0(A[4]), .in1(A[5]), .out(out[4]), .sel(Select));
  Multiplexer #(.enable("false")) multiplexer_6 (.in0(A[5]), .in1(A[6]), .out(out[5]), .sel(Select));
  Multiplexer #(.enable("false")) multiplexer_7 (.in0(A[6]), .in1(A[7]), .out(out[6]), .sel(Select));
  Multiplexer #(.enable("false")) multiplexer_8 (.in0(A[7]), .in1(A[8]), .out(out[7]), .sel(Select));
  Multiplexer #(.enable("false")) multiplexer_9 (.in0(A[8]), .in1(A[9]), .out(out[8]), .sel(Select));
  Multiplexer #(.enable("false")) multiplexer_10 (.in0(A[9]), .in1(A[10]), .out(out[9]), .sel(Select));
  Multiplexer #(.enable("false")) multiplexer_11 (.in0(A[10]), .in1(A[11]), .out(out[10]), .sel(Select));
  Multiplexer #(.enable("false")) multiplexer_12 (.in0(A[11]), .in1(A[12]), .out(out[11]), .sel(Select));
  Multiplexer #(.enable("false")) multiplexer_13 (.in0(A[12]), .in1(A[13]), .out(out[12]), .sel(Select));
  Multiplexer #(.enable("false")) multiplexer_14 (.in0(A[13]), .in1(A[14]), .out(out[13]), .sel(Select));
  Multiplexer #(.enable("false")) multiplexer_15 (.in0(A[14]), .in1(A[15]), .out(out[14]), .sel(Select));
  Multiplexer #(.enable("false")) multiplexer_16 (.in0(A[15]), .in1(A[16]), .out(out[15]), .sel(Select));
  Multiplexer #(.enable("false")) multiplexer_17 (.in0(A[16]), .in1(A[17]), .out(out[16]), .sel(Select));
  Multiplexer #(.enable("false")) multiplexer_18 (.in0(A[17]), .in1(A[18]), .out(out[17]), .sel(Select));
  Multiplexer #(.enable("false")) multiplexer_19 (.in0(A[18]), .in1(A[19]), .out(out[18]), .sel(Select));
  Multiplexer #(.enable("false")) multiplexer_20 (.in0(A[19]), .in1(A[20]), .out(out[19]), .sel(Select));
  Multiplexer #(.enable("false")) multiplexer_21 (.in0(A[20]), .in1(A[21]), .out(out[20]), .sel(Select));
  Multiplexer #(.enable("false")) multiplexer_22 (.in0(A[21]), .in1(A[22]), .out(out[21]), .sel(Select));
  Multiplexer #(.enable("false")) multiplexer_23 (.in0(A[22]), .in1(A[23]), .out(out[22]), .sel(Select));
  Multiplexer #(.enable("false")) multiplexer_24 (.in0(A[23]), .in1(A[24]), .out(out[23]), .sel(Select));
  Multiplexer #(.enable("false")) multiplexer_25 (.in0(A[24]), .in1(A[25]), .out(out[24]), .sel(Select));
  Multiplexer #(.enable("false")) multiplexer_26 (.in0(A[25]), .in1(A[26]), .out(out[25]), .sel(Select));
  Multiplexer #(.enable("false")) multiplexer_27 (.in0(A[26]), .in1(A[27]), .out(out[26]), .sel(Select));
  Multiplexer #(.enable("false")) multiplexer_28 (.in0(A[27]), .in1(A[28]), .out(out[27]), .sel(Select));
  Multiplexer #(.enable("false")) multiplexer_29 (.in0(A[28]), .in1(A[29]), .out(out[28]), .sel(Select));
  Multiplexer #(.enable("false")) multiplexer_30 (.in0(A[29]), .in1(A[30]), .out(out[29]), .sel(Select));
  Multiplexer #(.enable("false")) multiplexer_31 (.in0(A[30]), .in1(A[31]), .out(out[30]), .sel(Select));
  Multiplexer #(.enable("false")) multiplexer_32 (.in0(A[31]), .in1(B[0]), .out(out[31]), .sel(Select));
  Multiplexer #(.enable("false")) multiplexer_33 (.in0(B[0]), .in1(B[1]), .out(out_2[0]), .sel(Select));
  Multiplexer #(.enable("false")) multiplexer_34 (.in0(B[1]), .in1(B[2]), .out(out_2[1]), .sel(Select));
  Multiplexer #(.enable("false")) multiplexer_35 (.in0(B[2]), .in1(B[3]), .out(out_2[2]), .sel(Select));
  Multiplexer #(.enable("false")) multiplexer_36 (.in0(B[3]), .in1(B[4]), .out(out_2[3]), .sel(Select));
  Multiplexer #(.enable("false")) multiplexer_37 (.in0(B[4]), .in1(B[5]), .out(out_2[4]), .sel(Select));
  Multiplexer #(.enable("false")) multiplexer_38 (.in0(B[5]), .in1(B[6]), .out(out_2[5]), .sel(Select));
  Multiplexer #(.enable("false")) multiplexer_39 (.in0(B[6]), .in1(B[7]), .out(out_2[6]), .sel(Select));
  Multiplexer #(.enable("false")) multiplexer_40 (.in0(B[7]), .in1(B[8]), .out(out_2[7]), .sel(Select));
  Multiplexer #(.enable("false")) multiplexer_41 (.in0(B[8]), .in1(B[9]), .out(out_2[8]), .sel(Select));
  Multiplexer #(.enable("false")) multiplexer_42 (.in0(B[9]), .in1(B[10]), .out(out_2[9]), .sel(Select));
  Multiplexer #(.enable("false")) multiplexer_43 (.in0(B[10]), .in1(B[11]), .out(out_2[10]), .sel(Select));
  Multiplexer #(.enable("false")) multiplexer_44 (.in0(B[11]), .in1(B[12]), .out(out_2[11]), .sel(Select));
  Multiplexer #(.enable("false")) multiplexer_45 (.in0(B[12]), .in1(B[13]), .out(out_2[12]), .sel(Select));
  Multiplexer #(.enable("false")) multiplexer_46 (.in0(B[13]), .in1(B[14]), .out(out_2[13]), .sel(Select));
  Multiplexer #(.enable("false")) multiplexer_47 (.in0(B[14]), .in1(B[15]), .out(out_2[14]), .sel(Select));
  Multiplexer #(.enable("false")) multiplexer_48 (.in0(B[15]), .in1(B[16]), .out(out_2[15]), .sel(Select));
  Multiplexer #(.enable("false")) multiplexer_49 (.in0(B[16]), .in1(B[17]), .out(out_2[16]), .sel(Select));
  Multiplexer #(.enable("false")) multiplexer_50 (.in0(B[17]), .in1(B[18]), .out(out_2[17]), .sel(Select));
  Multiplexer #(.enable("false")) multiplexer_51 (.in0(B[18]), .in1(B[19]), .out(out_2[18]), .sel(Select));
  Multiplexer #(.enable("false")) multiplexer_52 (.in0(B[19]), .in1(B[20]), .out(out_2[19]), .sel(Select));
  Multiplexer #(.enable("false")) multiplexer_53 (.in0(B[20]), .in1(B[21]), .out(out_2[20]), .sel(Select));
  Multiplexer #(.enable("false")) multiplexer_54 (.in0(B[21]), .in1(B[22]), .out(out_2[21]), .sel(Select));
  Multiplexer #(.enable("false")) multiplexer_55 (.in0(B[22]), .in1(B[23]), .out(out_2[22]), .sel(Select));
  Multiplexer #(.enable("false")) multiplexer_56 (.in0(B[23]), .in1(B[24]), .out(out_2[23]), .sel(Select));
  Multiplexer #(.enable("false")) multiplexer_57 (.in0(B[24]), .in1(B[25]), .out(out_2[24]), .sel(Select));
  Multiplexer #(.enable("false")) multiplexer_58 (.in0(B[25]), .in1(B[26]), .out(out_2[25]), .sel(Select));
  Multiplexer #(.enable("false")) multiplexer_59 (.in0(B[26]), .in1(B[27]), .out(out_2[26]), .sel(Select));
  Multiplexer #(.enable("false")) multiplexer_60 (.in0(B[27]), .in1(B[28]), .out(out_2[27]), .sel(Select));
  Multiplexer #(.enable("false")) multiplexer_61 (.in0(B[28]), .in1(B[29]), .out(out_2[28]), .sel(Select));
  Multiplexer #(.enable("false")) multiplexer_62 (.in0(B[29]), .in1(B[30]), .out(out_2[29]), .sel(Select));
  Multiplexer #(.enable("false")) multiplexer_63 (.in0(B[30]), .in1(B[31]), .out(out_2[30]), .sel(Select));
  Multiplexer #(.enable("false")) multiplexer_64 (.in0(B[31]), .in1(1'b0), .out(out_2[31]), .sel(Select));
endmodule
