// Logisim project mult32.circ as structural Verilog: 1 circuit, main circuit main
module main (
  input  Start,
  input  [31:0] multiplicand,
  input  [31:0] multiplier,
  output done,
  output [31:0] product_31_16,
  output [31:0] product_15_0
);

  wire clock_1_out, datapath_1_comp, datapath_1_lsb, k_1_add, k_1_load, k_1_shift;

  Clock clock_1 (.out(clock_1_out));
  Datapath datapath_1 (
    .Multiplicand(multiplicand), .Multiplier(multiplier), .clock(clock_1_out), .add(k_1_add),
    .shift(k_1_shift), .comp(datapath_1_comp), .lsb(datapath_1_lsb), .load(k_1_load), .out_9(product_15_0),
    .out_10(product_31_16));
  k k_1 (
    .clock(clock_1_out), .st(Start), .lsb(datapath_1_lsb), .comp(datapath_1_comp), .load(k_1_load),
    .add(k_1_add), .shift(k_1_shift), .done(done));
endmodule
